# Fritzing sketch LINE FOLLOWER (saved by Fritzing 0.9.3b)

parts:
  Part1 = AF_mshield-v1.2_breadboard
  M1 = DC Motor
  M2 = DC Motor
  M3 = DC Motor
  M4 = DC Motor
  VCC1 = Battery
  Part4 = KY-033 Tracing Black White Line Hunting Sensor Module For Arduino
  Part5 = KY-033 Tracing Black White Line Hunting Sensor Module For Arduino
  Part6 = KY-033 Tracing Black White Line Hunting Sensor Module For Arduino

nets:
  GND: Part1.GND, VCC1.-, Part4.GND, Part5.GND, Part6.GND
  N1: Part1.V+, VCC1.+
  N2: Part1.1, Part5.S
  N3: Part1.4, Part6.S
  N4: Part1.6, Part4.S
  N5: Part1.VCC, Part4.V+, Part5.V+, Part6.V+
  N6: Part1.P1#166, M3.pin_2
  N7: Part1.P2#167, M3.pin_1
  N8: Part1.P4#169, M4.pin_2
  N9: Part1.P5#170, M4.pin_1
  N10: Part1.P1#171, M2.pin_2
  N11: Part1.P2#172, M2.pin_1
  N12: Part1.P4#174, M1.pin_2
  N13: Part1.P5#175, M1.pin_1

notes:
  LINE FOLLOWER
  designed by Hafis Novianas | date 26/01/23

custom parts:
  : motor Shield v1 Adafruit Adafruit Motor/Stepper/Servo Shield for Arduino kit [v1.2] : ID 81 : $19.50 : Adafruit Industries, Unique & fun DIY electronics and kits
  Battery: Your standard 2x 18650 battery pack (7,4 Volts)
  KY-033 Tracing Black White Line Hunting Sensor Module For Arduino: Tracing Black White Line Hunting Sensor Module For Arduino Description: This is KY-033 tracking sensor. The KY-033 measures the intensity of infrared radiation and delivers it as an analog output voltage. Features: Operating voltage: 2.5 - 12V(cannot over12V) working current: 18mA-20mA at 5V Enhanced accuracy Documents: http://www.vishay.com/docs/83760/tcrt5000.pdf

// code stored in the sketch: LINEFOLLOWER_TRIIPLESENSOR_without_for_LOGIC.ino
#include <AFMotor.h>
AF_DCMotor M1(3);
AF_DCMotor M2(4);
AF_DCMotor M3(1);
AF_DCMotor M4(2);

const int kiriSensor = A0;
const int tengahSensor = A3;
const int kananSensor =A5;
int a = 250;
int b = 220;
int c = 180; 
boolean kiriData, kananData, tengahData, before;
int i;
String binData;


void setup() {
    Serial.begin(9600);
    pinMode(kiriSensor, INPUT);
    pinMode(kananSensor, INPUT);
    pinMode(tengahSensor, INPUT);
    
     // turn on motor
    M1.setSpeed(a);
    M2.setSpeed(a);
    M3.setSpeed(a);
    M4.setSpeed(a);
    
    M1.run(RELEASE);
    M2.run(RELEASE);
    M3.run(RELEASE);
    M4.run(RELEASE);
}

void loop() {
  kiriData = digitalRead(kiriSensor);
  tengahData = digitalRead(tengahSensor);
  kananData = digitalRead(kananSensor);
  binData = String(kiriData)+String(tengahData)+String(kananData);
  //Serial.println(binData);

  if (binData == "000"){ //MEMORI
       Serial.println("000");
       if(before == 0){
          kanan();
       }
       if(before == 1){
          kiri();
       }
  }
  
  if (binData == "001"){ //KANAN
      Serial.println("001");
      kanan();
  }
  
  if (binData == "010"){ //MAJU
       Serial.println("010");
       i++;
       if(i<a){
          M1.setSpeed(i);
          M2.setSpeed(i);
          M3.setSpeed(i);
          M4.setSpeed(i);
       }
       
       M1.run(FORWARD);
       M2.run(FORWARD);
       M3.run(FORWARD);
       M4.run(FORWARD);
  }

  if (binData == "011"){ //KANAN
      Serial.println("011");
      kanan();
  }

  if (binData == "100"){ //KIRI
      Serial.println("100");
      kiri();
  }

  if (binData == "110"){ //KIRI
      Serial.println("110");
      kiri();
  }
  
  if (binData == "111"){ //MEMORI
       Serial.println("111");
       if(before == 0){
          kanan();
       }
       if(before == 1){
          kiri();
       }
  }
}

void kiri(){
      M1.setSpeed(b);
      M2.setSpeed(c);
      M3.setSpeed(c);
      M4.setSpeed(b);
      
      M1.run(FORWARD);
      M2.run(BACKWARD);
      M3.run(BACKWARD);
      M4.run(FORWARD);

      i = b;
      before = 1;
}

void kanan(){
      M1.setSpeed(c);
      M2.setSpeed(b);
      M3.setSpeed(b);
      M4.setSpeed(c);
      
      M1.run(BACKWARD);
      M2.run(FORWARD);
      M3.run(FORWARD);
      M4.run(BACKWARD);

      i = b;
      before = 0;
}

// code stored in the sketch: LINEFOLLOWER_TRIIPLESENSOR_without_for_LOGIC_inverse.ino
#include <AFMotor.h>

AF_DCMotor M1(1);
AF_DCMotor M2(2);
AF_DCMotor M3(3);
AF_DCMotor M4(4);

const int kiriSensor = A0;
const int tengahSensor = A3;
const int kananSensor = A5;
int a = 250;
int b = 200;
int c = 150; 
boolean kiriData, kananData, tengahData, before;
int i;
String binData;


void setup() {
    Serial.begin(9600);
    pinMode(kiriSensor, INPUT);
    pinMode(kananSensor, INPUT);
    pinMode(tengahSensor, INPUT);
    
     // turn on motor
    M1.setSpeed(a);
    M2.setSpeed(a);
    M3.setSpeed(a);
    M4.setSpeed(a);
    
    M1.run(RELEASE);
    M2.run(RELEASE);
    M3.run(RELEASE);
    M4.run(RELEASE);
}


void loop() {
  kiriData = digitalRead(kiriSensor);
  tengahData = digitalRead(tengahSensor);
  kananData = digitalRead(kananSensor);
  binData = String(kiriData)+String(tengahData)+String(kananData);
  Serial.println(binData);

  if (binData == "000"){ //MEMORI
       if(before == 0){
          kanan();
       }
       if(before == 1){
          kiri();
       }
  }
  
  if (binData == "110"){ //KANAN
      kanan();
  }
  
  if (binData == "101"){ //MAJU
       i++;
       if(i<a){
          M1.setSpeed(i);
          M2.setSpeed(i);
          M3.setSpeed(i);
          M4.setSpeed(i);
       }
       
       M1.run(FORWARD);
       M2.run(FORWARD);
       M3.run(FORWARD);
       M4.run(FORWARD);
  }

  if (binData == "100"){ //KANAN
      kanan();
  }

  if (binData == "011"){ //KIRI
      kiri();
  }

  if (binData == "001"){ //KIRI
      kiri();
  }
  
  if (binData == "111"){ //MEMORI 
       if(before == 0){
          kanan();
       }
       if(before == 1){
          kiri();
       }
  }
}

void kiri(){
      M1.setSpeed(b);
      M2.setSpeed(c);
      M3.setSpeed(c);
      M4.setSpeed(b);
      
      M1.run(FORWARD);
      M2.run(BACKWARD);
      M3.run(BACKWARD);
      M4.run(FORWARD);

      i = b;
      before = 1;
}

void kanan(){
      M1.setSpeed(c);
      M2.setSpeed(b);
      M3.setSpeed(b);
      M4.setSpeed(c);
      
      M1.run(BACKWARD);
      M2.run(FORWARD);
      M3.run(FORWARD);
      M4.run(BACKWARD);

      i = b;
      before = 0;
}
